# Fritzing sketch base board (saved by Fritzing 0.9.3b)
stripboards: 1

parts:
  Part1 = Arduino Nano (Rev3.0)
  Throttle_OUTPUT = female pin header, 1 pin [form="♀ (female)"]
  Receiver_Throttle = female pin header, 1 pin [form="♀ (female)"]
  Bluetooth = female pin header, 4 pins [form="♀ (female)"]
  Servo = female pin header, 3 pins [form="♀ (female)"]
  Sensor = female pin header, 3 pins [form="♀ (female)"]
  IC1 = IC, DIP package, 16 pins [chip_label=IC]

nets:
  N1: Part1.D1/TX, Bluetooth.pin4
  N2: Part1.D0/RX, Bluetooth.pin3
  N3: Part1.GND, Bluetooth.pin2, Servo.pin3, Sensor.pin3, IC1.pin1
  N4: Part1.D3, Servo.pin1
  N5: Part1.D4, IC1.pin16
  N6: Part1.D5, IC1.pin11
  N7: Part1.D6, IC1.pin10
  N8: Part1.5V, Bluetooth.pin1, Servo.pin2, Sensor.pin2, IC1.pin15
  N9: Part1.A0, Sensor.pin1
  N10: Throttle_OUTPUT.pin1, IC1.pin13
  N11: Receiver_Throttle.pin1, IC1.pin9
