# Fritzing sketch base board v2 (saved by Fritzing 0.9.3b)
circuit board: 7.54664cm x 4.75559cm
stripboards: 1

parts:
  Part1 = Arduino Nano (Rev3.0)
  ThO = female pin header, 1 pin [form="♀ (female)"]
  BT = female pin header, 4 pins [form="♀ (female)"]
  Sharp = female pin header, 3 pins [form="♀ (female)"]
  RL = IC, DIP package, 16 pins [chip_label=IC]
  US = female pin header, 4 pins [form="♀ (female)"]
  SRV = female pin header, 3 pins [form="♀ (female)"]
  RTh = female pin header, 1 pin [form="♀ (female)"]

nets:
  N1: Part1.D1/TX, BT.pin4
  N2: Part1.D0/RX, BT.pin3
  N3: Part1.GND, BT.pin2, Sharp.pin3, RL.pin1, US.pin4, SRV.pin3
  N4: Part1.D3, SRV.pin1
  N5: Part1.D7, Part1.D11/MOSI, RL.pin12, RL.pin16, US.pin3
  N6: Part1.D8, Part1.5V, BT.pin1, Sharp.pin2, RL.pin14, RL.pin15, US.pin1, US.pin2, SRV.pin2
  N7: Part1.D12/MISO, RL.pin6, RL.pin11
  N8: Part1.A0, Sharp.pin1
  N9: ThO.pin1, RL.pin13
  N10: RL.pin9, RTh.pin1
