# Fritzing sketch base board v3 (saved by Fritzing 0.9.3b)
circuit board: 7.54664cm x 4.75559cm
stripboards: 1

parts:
  Part1 = Arduino Nano (Rev3.0)
  ThO = female pin header, 1 pin [form="♀ (female)"]
  Sharp = female pin header, 3 pins [form="♀ (female)"]
  RL = IC, DIP package, 16 pins [chip_label=IC]
  US = female pin header, 4 pins [form="♀ (female)"]
  SRV = female pin header, 3 pins [form="♀ (female)"]
  RTh = female pin header, 1 pin [form="♀ (female)"]
  LSM = female pin header, 7 pins [form="♀ (female)"]
  Gyro = female pin header, 9 pins [form="♀ (female)"]
  BT = female pin header, 5 pins [form="♀ (female)"]
  R1 = Resistor [tolerance=±5% resistance=470 package=THT]
  RX_IN = female pin header, 1 pin [form="♀ (female)"]
  PWR = female pin header, 2 pins [form="♀ (female)"]
  LED1 = LED - 3mm [color="Red (633nm)" package="3 mm [THT]"]

nets:
  N1: Part1.D1/TX, BT.pin4
  N2: Part1.D0/RX, BT.pin3
  N3: Part1.GND, Sharp.pin3, RL.pin1, US.pin4, SRV.pin3, LSM.pin2, Gyro.pin3, BT.pin2, R1.Pin_1, PWR.pin2
  N4: Part1.D3, SRV.pin1
  N5: Part1.D4, RX_IN.pin1
  N6: Part1.D7, US.pin3
  N7: Part1.D8, US.pin2
  N8: Part1.D11/MOSI, RL.pin16
  N9: Part1.D12/MISO, RL.pin11
  N10: Part1.5V, Sharp.pin2, US.pin1, SRV.pin2, LSM.pin1, Gyro.pin1, BT.pin1, PWR.pin1
  N11: Part1.A5, LSM.pin7, Gyro.pin9
  N12: Part1.A4, LSM.pin6, Gyro.pin8
  N13: Part1.A0, Sharp.pin1
  N14: ThO.pin1, RL.pin13
  N15: RL.pin9, RTh.pin1
  N16: BT.pin5, LED1.anode
  N17: R1.Pin_0, LED1.cathode
